// Logisim project 2nd session MERL.circ as structural Verilog: 4 circuits, main circuit main
module main (
  input  in_1,
  input  in_2,
  input  in_3,
  input  in_4,
  input  [1:0] in_5,
  output out_6
);

  _4_bit_MUX u_4_bit_mux_1 (.D(in_4), .B(in_2), .C(in_3), .A(in_1), .out_6(out_6), .in_5(in_5));
endmodule

module _2_bit_MUX (
  input  in_1,
  input  in_2,
  input  in_3,
  output out_4
);

  wire nand_1_out, nand_2_out, nand_3_out;

  nand nand_1 (nand_1_out, in_2, in_2);
  nand nand_2 (nand_2_out, in_1, in_2);
  nand nand_3 (nand_3_out, nand_1_out, in_3);
  nand nand_4 (out_4, nand_2_out, nand_3_out);
endmodule

module _4_bit_MUX (
  input  D,
  input  B,
  input  C,
  input  A,
  input  [1:0] in_5,
  output out_6
);

  wire n2_bit_mux_1_out_4, n2_bit_mux_2_out_4;

  _2_bit_MUX u_2_bit_mux_1 (.in_1(D), .in_2(in_5[1]), .in_3(B), .out_4(n2_bit_mux_1_out_4));
  _2_bit_MUX u_2_bit_mux_2 (.in_1(C), .in_2(in_5[1]), .in_3(A), .out_4(n2_bit_mux_2_out_4));
  _2_bit_MUX u_2_bit_mux_3 (.in_1(n2_bit_mux_1_out_4), .in_2(in_5[0]), .in_3(n2_bit_mux_2_out_4), .out_4(out_6));
endmodule

module _1_bit_comparator (
  input  A,
  input  B,
  output A_B,
  output A_B_2,
  output A_B_3
);

  wire not_1_out, not_2_out;

  not not_1 (not_1_out, B);
  not not_2 (not_2_out, A);
  and and_1 (A_B, A, not_1_out);
  xnor xnor_1 (A_B_2, A, B);
  and and_2 (A_B_3, not_2_out, B);
endmodule
