// Logisim project 4x1mux.circ as structural Verilog: 1 circuit, main circuit main
module main (
  input  D,
  input  C,
  input  B,
  input  A,
  input  [1:0] sel,
  output \output 
);

  wire main_1_p4, main_2_p3;

  // _2x1mux_main main_1: pin names not known; wires that end beside it: D, C, sel[0], main_1_p4
  // _2x1mux_main main_2: pin names not known; wires that end beside it: B, A, main_2_p3
  // _2x1mux_main main_3: pin names not known; wires that end beside it: main_1_p4, main_2_p3, sel[1], \output 
endmodule
